# Fritzing sketch Sensor (saved by Fritzing 0.7.11b)
breadboards: 1

parts:
  U1 = Arduino Mega
  R1 = Resistor [tolerance=±5% resistance=1M package=THT]
  R2 = Resistor [tolerance=±5% resistance=1M package=THT]
  R3 = Resistor [tolerance=±5% resistance=1M package=THT]
  LED1 = LED - 5mm [color="Red (633nm)" package="5 mm [THT]"]
  LED2 = LED - 5mm [color="Red (633nm)" package="5 mm [THT]"]
  LED3 = LED - 5mm [color="Red (633nm)" package="5 mm [THT]"]
  R4 = Resistor [tolerance=±5% resistance=220 package=THT]
  R5 = Resistor [tolerance=±5% resistance=220 package=THT]
  R6 = Resistor [tolerance=±5% resistance=220 package=THT]

nets:
  N1: U1.+5V, R1.Pin_1, R2.Pin_1, R3.Pin_1
  N2: U1.GND, R4.Pin_1, R5.Pin_1, R6.Pin_1
  N3: U1.A0, R3.Pin_0
  N4: U1.A1, R2.Pin_0
  N5: U1.A2, R1.Pin_0
  N6: U1.D49, LED1.cathode
  N7: U1.D51, LED2.cathode
  N8: U1.D53, LED3.cathode
  N9: LED1.anode, R4.Pin_0
  N10: LED2.anode, R5.Pin_0
  N11: LED3.anode, R6.Pin_0

notes:
  Cups attached to A0-A2
